# Fritzing sketch Delay USB (saved by Fritzing 0.9.4)
circuit board: 3.3003cm x 1.63678cm

parts:
  Q1 = Basic FET N-Channel [package="DPak [SMD]"]
  Power_plug_IN = Power plug
  R1 = Resistor [tolerance=±5% resistance=100 package="0805 [SMD]"]
  Power_plug_OUT = Power plug
  R2 = Resistor [tolerance=±5% resistance=10k package="0805 [SMD]"]
  R3 = Resistor [tolerance=±5% resistance=220 package="0805 [SMD]"]
  U1 = ATTINY13 [package=so]
  S2 = SWITCH-MOMENTARY-2 [package=tactile-switch-1101ne]
  R4 = Resistor [tolerance=±5% resistance=330 package="0805 [SMD]"]
  R5 = Resistor [tolerance=±5% resistance=10k package="0805 [SMD]"]
  R6 = Resistor [tolerance=±5% resistance=330 package="0805 [SMD]"]
  LED2 = LEDs [package=led-1206]
  LED3 = LEDs [package=led-1206]

nets:
  N1: Q1.Gate, R1.Pin_1, R2.Pin_1
  N2: Q1.drain, Power_plug_OUT.GND, LED3.C
  GND: Q1.source, Power_plug_IN.GND, R2.Pin_0, U1.GND, S2.2
  VCC: Power_plug_IN.VCC, Power_plug_OUT.VCC, U1.VCC, R5.Pin_1, R6.Pin_1, LED2.A
  N3: R1.Pin_0, U1.PB0(MOSI)
  N4: R3.Pin_0, U1.PB2(SCK_ADC1)
  N5: R3.Pin_1, LED2.C
  N6: U1.PB4(ADC2), R4.Pin_1, R5.Pin_0
  N7: S2.1, R4.Pin_0
  N8: R6.Pin_0, LED3.A

notes:
  Power 5V
  R1 100 Ом
  R2 10 кОм
  R3 220 Ом
  R4 300-500 Ом
  R5 10-100кОм
  R6 220-2000 Ом
  Q1 IRLR8726PBF (IRF3205)
  R2
  R1
  Power IN
  Power OUT
  Q1
  R3
  LED1
  pushButton
  Attiny13 SOP8
  IN VCC
  OUT VCC
  R4
  R5
  LED2
  R6
